// Logisim project CPU.circ as structural Verilog: 6 circuits, main circuit main
module main (
  input  RESET
);

  wire alu_1_zero, CLK_out, not_1_out, undriven;
  wire [4:0] decode_1_addr_in, decode_1_addr_out1, decode_1_addr_out2;
  wire [5:0] decode_1_pla_out;
  wire [7:0] alu_1_s;
  wire [31:0] data_memory_1_data_out, decode_1_mux_out, multiplexer_1_out, multiplexer_2_out,
       program_memory_1_instruction, registers_1_data_out1, registers_1_data_out2;
  wire [31:8] alu_1_s_2;

  Clock CLK (.out(CLK_out));
  Program_Memory program_memory_1 (
    .CLK(CLK_out), .PC_RST(RESET), .Instruction(program_memory_1_instruction));  // open: Jmp_Addr, Jmp_Select
  Decode decode_1 (
    .Instruction(program_memory_1_instruction), .PLA_Out(decode_1_pla_out), .Addr_in(decode_1_addr_in),
    .Addr_Out2(decode_1_addr_out2), .Addr_Out1(decode_1_addr_out1), .MUX_Out(decode_1_mux_out));
  Multiplexer #(.width(32)) multiplexer_1 (
    .in0({alu_1_s_2, alu_1_s}), .in1(data_memory_1_data_out), .out(multiplexer_1_out),
    .sel(decode_1_pla_out[4]));
  not not_1 (not_1_out, decode_1_pla_out[3]);
  Registers registers_1 (
    .Addr_out2(decode_1_addr_out2), .Addr_out1(decode_1_addr_out1), .Data_in(multiplexer_1_out),
    .Addr_in(decode_1_addr_in), .Clk(CLK_out), .Reset(RESET), .Data_out2(registers_1_data_out2),
    .Data_out1(registers_1_data_out1));
  Multiplexer #(.width(32)) multiplexer_2 (
    .in0(decode_1_mux_out), .in1(registers_1_data_out2), .out(multiplexer_2_out), .sel(not_1_out));
  ALU alu_1 (
    .OpCode(decode_1_pla_out[2:0]), .OP1(multiplexer_2_out), .OP2(registers_1_data_out1),
    .S({alu_1_s_2, alu_1_s}), .Zero(alu_1_zero));
  Data_Memory data_memory_1 (
    .Addr(alu_1_s), .Enable(undriven), .Read_Write(decode_1_pla_out[5]), .Clk(CLK_out),
    .Data_In(registers_1_data_out2), .Data_Out(data_memory_1_data_out));
endmodule

module Registers (
  input  [4:0] Addr_out2,
  input  [4:0] Addr_out1,
  input  [31:0] Data_in,
  input  [4:0] Addr_in,
  input  Clk,
  input  Reset,
  output [31:0] Data_out2,
  output [31:0] Data_out1
);

  wire decoder_1_out1, decoder_1_out2, decoder_1_out3, decoder_1_out4, decoder_1_out5, decoder_1_out6,
       decoder_1_out7, decoder_1_out8, decoder_1_out9, decoder_1_out10, decoder_1_out11, decoder_1_out12,
       decoder_1_out13, decoder_1_out14, decoder_1_out15, decoder_1_out16, decoder_1_out17, decoder_1_out18,
       decoder_1_out19, decoder_1_out20, decoder_1_out21, decoder_1_out22, decoder_1_out23, decoder_1_out24,
       decoder_1_out25, decoder_1_out26, decoder_1_out27, decoder_1_out28, decoder_1_out29, decoder_1_out30,
       decoder_1_out31;
  wire [31:0] x1_q, x2_q, x3_q, x4_q, x5_q, x6_q, x7_q, x8_q, x9_q, x10_q, x11_q, x12_q, x13_q, x14_q, x15_q,
       x16_q, x17_q, x18_q, x19_q, x20_q, x21_q, x22_q, x23_q, x24_q, x25_q, x26_q, x27_q, x28_q, x29_q,
       x30_q, x31_q;

  Decoder #(.select(5)) decoder_1 (
    .out1(decoder_1_out1), .out2(decoder_1_out2), .out3(decoder_1_out3), .out4(decoder_1_out4),
    .out5(decoder_1_out5), .out6(decoder_1_out6), .out7(decoder_1_out7), .out8(decoder_1_out8),
    .out9(decoder_1_out9), .out10(decoder_1_out10), .out11(decoder_1_out11), .out12(decoder_1_out12),
    .out13(decoder_1_out13), .out14(decoder_1_out14), .out15(decoder_1_out15), .out16(decoder_1_out16),
    .out17(decoder_1_out17), .out18(decoder_1_out18), .out19(decoder_1_out19), .out20(decoder_1_out20),
    .out21(decoder_1_out21), .out22(decoder_1_out22), .out23(decoder_1_out23), .out24(decoder_1_out24),
    .out25(decoder_1_out25), .out26(decoder_1_out26), .out27(decoder_1_out27), .out28(decoder_1_out28),
    .out29(decoder_1_out29), .out30(decoder_1_out30), .out31(decoder_1_out31), .sel(Addr_in), .en(1'b1));  // open: out0
  Register #(.trigger("falling"), .width(32)) x31 (
    .D(Data_in), .en(decoder_1_out31), .clk(Clk), .Q(x31_q), .clr(Reset));
  Register #(.trigger("falling"), .width(32)) x30 (
    .D(Data_in), .en(decoder_1_out30), .clk(Clk), .Q(x30_q), .clr(Reset));
  Register #(.trigger("falling"), .width(32)) x29 (
    .D(Data_in), .en(decoder_1_out29), .clk(Clk), .Q(x29_q), .clr(Reset));
  Register #(.trigger("falling"), .width(32)) x28 (
    .D(Data_in), .en(decoder_1_out28), .clk(Clk), .Q(x28_q), .clr(Reset));
  Register #(.trigger("falling"), .width(32)) x27 (
    .D(Data_in), .en(decoder_1_out27), .clk(Clk), .Q(x27_q), .clr(Reset));
  Register #(.trigger("falling"), .width(32)) x26 (
    .D(Data_in), .en(decoder_1_out26), .clk(Clk), .Q(x26_q), .clr(Reset));
  Register #(.trigger("falling"), .width(32)) x25 (
    .D(Data_in), .en(decoder_1_out25), .clk(Clk), .Q(x25_q), .clr(Reset));
  Register #(.trigger("falling"), .width(32)) x24 (
    .D(Data_in), .en(decoder_1_out24), .clk(Clk), .Q(x24_q), .clr(Reset));
  Register #(.trigger("falling"), .width(32)) x23 (
    .D(Data_in), .en(decoder_1_out23), .clk(Clk), .Q(x23_q), .clr(Reset));
  Register #(.trigger("falling"), .width(32)) x22 (
    .D(Data_in), .en(decoder_1_out22), .clk(Clk), .Q(x22_q), .clr(Reset));
  Register #(.trigger("falling"), .width(32)) x21 (
    .D(Data_in), .en(decoder_1_out21), .clk(Clk), .Q(x21_q), .clr(Reset));
  Register #(.trigger("falling"), .width(32)) x20 (
    .D(Data_in), .en(decoder_1_out20), .clk(Clk), .Q(x20_q), .clr(Reset));
  Register #(.trigger("falling"), .width(32)) x19 (
    .D(Data_in), .en(decoder_1_out19), .clk(Clk), .Q(x19_q), .clr(Reset));
  Register #(.trigger("falling"), .width(32)) x18 (
    .D(Data_in), .en(decoder_1_out18), .clk(Clk), .Q(x18_q), .clr(Reset));
  Register #(.trigger("falling"), .width(32)) x17 (
    .D(Data_in), .en(decoder_1_out17), .clk(Clk), .Q(x17_q), .clr(Reset));
  Register #(.trigger("falling"), .width(32)) x16 (
    .D(Data_in), .en(decoder_1_out16), .clk(Clk), .Q(x16_q), .clr(Reset));
  Register #(.trigger("falling"), .width(32)) x15 (
    .D(Data_in), .en(decoder_1_out15), .clk(Clk), .Q(x15_q), .clr(Reset));
  Register #(.trigger("falling"), .width(32)) x14 (
    .D(Data_in), .en(decoder_1_out14), .clk(Clk), .Q(x14_q), .clr(Reset));
  Register #(.trigger("falling"), .width(32)) x13 (
    .D(Data_in), .en(decoder_1_out13), .clk(Clk), .Q(x13_q), .clr(Reset));
  Register #(.trigger("falling"), .width(32)) x12 (
    .D(Data_in), .en(decoder_1_out12), .clk(Clk), .Q(x12_q), .clr(Reset));
  Register #(.trigger("falling"), .width(32)) x11 (
    .D(Data_in), .en(decoder_1_out11), .clk(Clk), .Q(x11_q), .clr(Reset));
  Register #(.trigger("falling"), .width(32)) x10 (
    .D(Data_in), .en(decoder_1_out10), .clk(Clk), .Q(x10_q), .clr(Reset));
  Register #(.trigger("falling"), .width(32)) x9 (.D(Data_in), .en(decoder_1_out9), .clk(Clk), .Q(x9_q), .clr(Reset));
  Register #(.trigger("falling"), .width(32)) x8 (.D(Data_in), .en(decoder_1_out8), .clk(Clk), .Q(x8_q), .clr(Reset));
  Register #(.trigger("falling"), .width(32)) x7 (.D(Data_in), .en(decoder_1_out7), .clk(Clk), .Q(x7_q), .clr(Reset));
  Register #(.trigger("falling"), .width(32)) x6 (.D(Data_in), .en(decoder_1_out6), .clk(Clk), .Q(x6_q), .clr(Reset));
  Register #(.trigger("falling"), .width(32)) x5 (.D(Data_in), .en(decoder_1_out5), .clk(Clk), .Q(x5_q), .clr(Reset));
  Register #(.trigger("falling"), .width(32)) x4 (.D(Data_in), .en(decoder_1_out4), .clk(Clk), .Q(x4_q), .clr(Reset));
  Register #(.trigger("falling"), .width(32)) x3 (.D(Data_in), .en(decoder_1_out3), .clk(Clk), .Q(x3_q), .clr(Reset));
  Register #(.trigger("falling"), .width(32)) x2 (.D(Data_in), .en(decoder_1_out2), .clk(Clk), .Q(x2_q), .clr(Reset));
  Register #(.trigger("falling"), .width(32)) x1 (.D(Data_in), .en(decoder_1_out1), .clk(Clk), .Q(x1_q), .clr(Reset));
  Multiplexer #(.select(5), .width(32)) multiplexer_1 (
    .in0({32{1'b0}}), .in1(x1_q), .in2(x2_q), .in3(x3_q), .in4(x4_q), .in5(x5_q), .in6(x6_q), .in7(x7_q),
    .in8(x8_q), .in9(x9_q), .in10(x10_q), .in11(x11_q), .in12(x12_q), .in13(x13_q), .in14(x14_q),
    .in15(x15_q), .in16(x16_q), .in17(x17_q), .in18(x18_q), .in19(x19_q), .in20(x20_q), .in21(x21_q),
    .in22(x22_q), .in23(x23_q), .in24(x24_q), .in25(x25_q), .in26(x26_q), .in27(x27_q), .in28(x28_q),
    .in29(x29_q), .in30(x30_q), .in31(x31_q), .out(Data_out2), .sel(Addr_out2));
  Multiplexer #(.select(5), .width(32)) multiplexer_2 (
    .in0({32{1'b0}}), .in1(x1_q), .in2(x2_q), .in3(x3_q), .in4(x4_q), .in5(x5_q), .in6(x6_q), .in7(x7_q),
    .in8(x8_q), .in9(x9_q), .in10(x10_q), .in11(x11_q), .in12(x12_q), .in13(x13_q), .in14(x14_q),
    .in15(x15_q), .in16(x16_q), .in17(x17_q), .in18(x18_q), .in19(x19_q), .in20(x20_q), .in21(x21_q),
    .in22(x22_q), .in23(x23_q), .in24(x24_q), .in25(x25_q), .in26(x26_q), .in27(x27_q), .in28(x28_q),
    .in29(x29_q), .in30(x30_q), .in31(x31_q), .out(Data_out1), .sel(Addr_out1));

  // Notes on the sheet:
  //   x0
endmodule

module ALU (
  input  [2:0] OpCode,
  input  [31:0] OP1,
  input  [31:0] OP2,
  output [31:0] S,
  output Zero
);

  wire [31:0] adder_1_out, and_1_out, or_1_out, subtractor_1_out, xor_1_out;

  Adder #(.width(32)) adder_1 (.a(OP1), .b(OP2), .out(adder_1_out));  // open: cin, cout
  Subtractor #(.width(32)) subtractor_1 (.a(OP1), .b(OP2), .out(subtractor_1_out));  // open: bin, bout
  assign xor_1_out = OP1 ^ OP2;  // XOR_Gate xor_1, 32 bits wide
  assign and_1_out = OP1 & OP2;  // AND_Gate and_1, 32 bits wide
  assign or_1_out = OP1 | OP2;  // OR_Gate or_1, 32 bits wide
  Multiplexer #(.select(3), .width(32)) multiplexer_1 (
    .in0({32{1'b0}}), .in1(adder_1_out), .in2(subtractor_1_out), .in3(xor_1_out), .in4(and_1_out),
    .in5(or_1_out), .out(S), .sel(OpCode));  // open: in6, in7
  Comparator #(.mode("unsigned"), .width(32)) comparator_1 (.a(S), .b({32{1'b0}}), .eq(Zero));  // open: gt, lt
endmodule

module Program_Memory (
  input  [7:0] Jmp_Addr,
  input  Jmp_Select,
  input  CLK,
  input  PC_RST,
  output [31:0] Instruction
);

  wire or_1_out;
  wire [7:0] adder_1_out, PC_q;

  Adder adder_1 (.a({8{1'b0}}), .b(PC_q), .out(adder_1_out), .cin(1'b1));  // open: cout
  Register PC (.D(adder_1_out), .en(1'b1), .clk(CLK), .Q(PC_q), .clr(PC_RST));
  RAM #(.dataWidth(32), .trigger("falling")) PROM (
    .addr(PC_q), .we(1'b0), .oe(1'b1), .clk(or_1_out), .dout(Instruction));  // open: din
  or or_1 (or_1_out, CLK, PC_RST);
endmodule

module Decode (
  input  [31:0] Instruction,
  output [5:0] PLA_Out,
  output [4:0] Addr_in,
  output [4:0] Addr_Out2,
  output [4:0] Addr_Out1,
  output [31:0] MUX_Out
);

  wire undriven;

  PLA #(.in_width(17), .out_width(6), .\table ("00000000000110011 000001 # ADD\nxxxxxxx0000010011 001001 # ADDI\n01000000000110011 000010 # SUB\n00000001110110011 000011 # AND\n00000001100110011 000100 # OR\n00000001000110011 000101 # XOR")) pla_1 (
    .in({Instruction[31:25], Instruction[14:12], Instruction[6:0]}), .out(PLA_Out));
  Multiplexer #(.width(32)) multiplexer_1 (
    .in0({{20{1'b0}}, Instruction[31:20]}), .in1({{20{1'b0}}, Instruction[31:25], Instruction[11:7]}),
    .out(MUX_Out), .sel(undriven));

  assign Addr_in = Instruction[11:7];
  assign Addr_Out1 = Instruction[19:15];
  assign Addr_Out2 = Instruction[24:20];
endmodule

module Data_Memory (
  input  [7:0] Addr,
  input  Enable,
  input  Read_Write,
  input  Clk,
  input  [31:0] Data_In,
  output [31:0] Data_Out
);

  wire and_1_out, not_1_out;

  RAM #(.dataWidth(32)) ram_1 (
    .addr(Addr), .we(Read_Write), .oe(not_1_out), .clk(and_1_out), .din(Data_In), .dout(Data_Out));
  not not_1 (not_1_out, Read_Write);
  and and_1 (and_1_out, Clk, Enable);
endmodule
